# Fritzing sketch STM32_TrafikLambasi.pdsprj (saved by Fritzing 0.9.4)
breadboards: 1

parts:
  LED1 = smd LED [color="Red (633nm)" package="1206 [SMD]"]
  LED2 = smd LED [color="Yellow (595nm)" package="1206 [SMD]"]
  LED3 = smd LED [color="Green (560nm)" package="1206 [SMD]"]
  R1 = Resistor [tolerance=±5% resistance=110 package="0805 [SMD]"]
  R2 = Resistor [tolerance=±5% resistance=110 package="0805 [SMD]"]
  R3 = Resistor [tolerance=±5% resistance=110 package="0805 [SMD]"]
  Parça1 = BluePill

nets:
  N1: LED1.anode, LED2.anode, LED3.anode, Parça1.5V
  N2: R1.Pin_0, Parça1.B15
  N3: R2.Pin_0, Parça1.B14
  N4: R3.Pin_0, Parça1.B13
